# Fritzing sketch v4-weight-sensor (saved by Fritzing 0.9.3b)

parts:
  Load_Cell1 = Load Cell - Red/white/black/green
  Part1 = HX711 Weighing Sensor Module
  U1 = NodeMCU V1.0

nets:
  N1: Load_Cell1.wire1, Part1.E+
  N2: Load_Cell1.wire2, Part1.A-, U1.3V3
  N3: Load_Cell1.wire3, Part1.E-
  N4: Load_Cell1.wire4, Part1.A+
  VCC: Part1.VCC, U1.Vin
  GND: Part1.GND, U1.GND
  N5: Part1.DO/RX, U1.D6
  N6: Part1.CK/TX, U1.D5

custom parts:
  Load Cell - Red/white/black/green: A rectangle load cell/weighting pressure Sensor with four wires - Red, white, black, green. Normally corresponding with E+, E-, A+, A- respectively.
  NodeMCU V1.0: ESP8266 based NodeMCU
